# Fritzing sketch coaster (saved by Fritzing 0.9.3b)
circuit board: 11.5cm x 11.5cm

parts:
  NANO_33_IoT = Arduino Nano 33 IOT
  RED1 = LED - 5mm [color="Red (633nm)" package="5 mm [THT]"]
  RED2 = LED - 5mm [color="Red (633nm)" package="5 mm [THT]"]
  RED3 = LED - 5mm [color="Red (633nm)" package="5 mm [THT]"]
  RED4 = LED - 5mm [color="Red (633nm)" package="5 mm [THT]"]
  RED5 = LED - 5mm [color="Red (633nm)" package="5 mm [THT]"]
  RED7 = LED - 5mm [color="Red (633nm)" package="5 mm [THT]"]
  RED8 = LED - 5mm [color="Red (633nm)" package="5 mm [THT]"]
  GREEN1 = LED - 5mm [color="Red (633nm)" package="5 mm [THT]"]
  GREEN2 = LED - 5mm [color="Red (633nm)" package="5 mm [THT]"]
  GREEN5 = LED - 5mm [color="Red (633nm)" package="5 mm [THT]"]
  GREEN5_2 = LED - 5mm [color="Red (633nm)" package="5 mm [THT]"]
  GREEN6 = LED - 5mm [color="Red (633nm)" package="5 mm [THT]"]
  GREEN7 = LED - 5mm [color="Red (633nm)" package="5 mm [THT]"]
  GREEN8 = LED - 5mm [color="Red (633nm)" package="5 mm [THT]"]
  BLUE1 = LED - 5mm [color="Red (633nm)" package="5 mm [THT]"]
  BLUE2 = LED - 5mm [color="Red (633nm)" package="5 mm [THT]"]
  BLUE3 = LED - 5mm [color="Red (633nm)" package="5 mm [THT]"]
  BLUE4 = LED - 5mm [color="Red (633nm)" package="5 mm [THT]"]
  BLUE5 = LED - 5mm [color="Red (633nm)" package="5 mm [THT]"]
  BLUE6 = LED - 5mm [color="Red (633nm)" package="5 mm [THT]"]
  BLUE7 = LED - 5mm [color="Red (633nm)" package="5 mm [THT]"]
  BLUE8 = LED - 5mm [color="Red (633nm)" package="5 mm [THT]"]
  VCC1 = Battery
  GREEN3 = LED - 5mm [color="Red (633nm)" package="5 mm [THT]"]
  WHITE1 = LED - 5mm [color="Red (633nm)" package="5 mm [THT]"]
  WHITE2 = LED - 5mm [color="Red (633nm)" package="5 mm [THT]"]
  WHITE3 = LED - 5mm [color="Red (633nm)" package="5 mm [THT]"]
  WHITE4 = LED - 5mm [color="Red (633nm)" package="5 mm [THT]"]
  RED6 = LED - 5mm [color="Red (633nm)" package="5 mm [THT]"]
  WHITE6 = LED - 5mm [color="Red (633nm)" package="5 mm [THT]"]
  WHITE7 = LED - 5mm [color="Red (633nm)" package="5 mm [THT]"]
  WHITE8 = LED - 5mm [color="Red (633nm)" package="5 mm [THT]"]
  WHITE5 = LED - 5mm [color="Red (633nm)" package="5 mm [THT]"]

nets:
  N1: NANO_33_IoT.GND, RED1.cathode, RED2.cathode, RED3.cathode, RED4.cathode, RED5.cathode, RED7.cathode, RED8.cathode, GREEN1.cathode, GREEN2.cathode, GREEN5.cathode, GREEN5_2.cathode, GREEN6.cathode, GREEN7.cathode, GREEN8.cathode, BLUE1.cathode, BLUE2.cathode, BLUE3.cathode, BLUE4.cathode, BLUE5.cathode, BLUE6.cathode, BLUE7.cathode, BLUE8.cathode, VCC1.-, GREEN3.cathode, WHITE1.cathode, WHITE2.cathode, WHITE3.cathode, WHITE4.cathode, RED6.cathode, WHITE6.cathode, WHITE7.cathode, WHITE8.cathode, WHITE5.cathode
  N2: NANO_33_IoT.D10~, BLUE1.anode, BLUE2.anode, BLUE3.anode, BLUE4.anode, BLUE5.anode, BLUE6.anode, BLUE7.anode, BLUE8.anode
  N3: NANO_33_IoT.D11/MOSI, GREEN1.anode, GREEN2.anode, GREEN5.anode, GREEN5_2.anode, GREEN6.anode, GREEN7.anode, GREEN8.anode, GREEN3.anode
  N4: NANO_33_IoT.D12~/MISO, RED1.anode, RED2.anode, RED3.anode, RED4.anode, RED5.anode, RED7.anode, RED8.anode, RED6.anode
  N5: NANO_33_IoT.VIN, VCC1.+
  N6: NANO_33_IoT.A2, WHITE1.anode, WHITE2.anode, WHITE3.anode, WHITE4.anode, WHITE6.anode, WHITE7.anode, WHITE8.anode, WHITE5.anode

notes:
  GND
  VIN

custom parts:
  Arduino Nano 33 IOT: The Arduino Nano 33 IoT is the easiest and cheapest point of entry to enhance existing devices (and creating new ones) to be part of the IoT and designing pico-network applications. Whether you are looking at building a sensor network connected to your office or home router, or if you want to create a BLE device sending data to a cellphone, the Nano 33 IoT is your one-stop-solution for many of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
